# Fritzing sketch 20230321_motor (saved by Fritzing 0.9.10b)
breadboards: 1

parts:
  부품1 = Arduino Mega 2560 (Rev3)
  HC-SR04_Sensor_1 = HC-SR04 Ultrasonic Distance Sensor
  HC-SR04_Sensor_2 = HC-SR04 Ultrasonic Distance Sensor
  HC-SR04_Sensor_3 = HC-SR04 Ultrasonic Distance Sensor
  L298N2 = L298N DC motor driver
  VCC1 = Battery

nets:
  N1: 부품1.D13_PWM, L298N2.ENB
  N2: 부품1.D12_PWM, L298N2.IN4
  N3: 부품1.D11_PWM, L298N2.IN3
  N4: 부품1.D10_PWM, L298N2.IN2
  N5: 부품1.D9_PWM, L298N2.IN1
  N6: 부품1.D8_PWM, L298N2.ENA
  VCC: 부품1.5V, HC-SR04_Sensor_1.VCC, HC-SR04_Sensor_2.VCC, HC-SR04_Sensor_3.VCC, L298N2.5V
  GND: 부품1.GND, HC-SR04_Sensor_1.GND, HC-SR04_Sensor_2.GND, HC-SR04_Sensor_3.GND, L298N2.GND, VCC1.-
  N7: 부품1.D2_PWM, HC-SR04_Sensor_1.TRIG
  N8: 부품1.D3_PWM, HC-SR04_Sensor_1.ECHO
  N9: 부품1.D4_PWM, HC-SR04_Sensor_2.TRIG
  N10: 부품1.D5_PWM, HC-SR04_Sensor_2.ECHO
  N11: 부품1.D6_PWM, HC-SR04_Sensor_3.TRIG
  N12: 부품1.D7_PWM, HC-SR04_Sensor_3.ECHO
  N13: L298N2.12V, VCC1.+

custom parts:
  L298N DC motor driver: 2x DC motor driver with 78M05 positive voltage regulator (7..35 V) L298N: max 46 V, 2 A Set 5 V Enable jumper to enable 5 V regultor (needed for the L298N) and +5 V output at screw terminal or supply external +5 V at screw terminal Set ENA and/or ENB to +5 V to enable motor permanently or supply ENA and/or ENB with PWM signal IN1 and IN2 set rotation directory for motor A (OUT1/OUT2) IN2 and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
  Battery: Your standard 2x 18650 battery pack (7,4 Volts)
